// Logisim project CS1501_U201514477_华龙_cpu.circ as structural Verilog: 4 circuits, main circuit MIPS CPU
module MIPS_CPU (
);

  wire ALU_Equal, ALU_R_0, and_3_out, and_4_out, and_5_out, beq, bltz, bne, branch, clk, clock_1_out,
       d_ff_1_qn, d_ff_2_qn, d_ff_3_qn, d_ff_4_qn, display__a0, halt, nor_1_out, nor_2_out, not_1_out,
       not_2_out, not_3_out, RST, \单步执行_out ;
  wire [3:0] ALUOP;
  wire [4:0] multiplexer_4_out, multiplexer_8_out, multiplexer_9_out, multiplexer_10_out;
  wire [9:0] PC_q_2;
  wire [15:0] multiplexer_17_out, \总周期数 , \无条件分支指令数 , \有条件分支成功跳转 , \有条件分支指令数 ;
  wire [16:0] multiplexer_5_out, multiplexer_6_out, multiplexer_11_out;
  wire [23:0] alu_1_result_2, control_signal;
  wire [27:2] rom_1_data;
  wire [31:0] bit_extender_1_out, branch_addr, mips_ram_1_p6, multiplexer_1_out, multiplexer_2_out,
       multiplexer_3_out, multiplexer_7_out, multiplexer_12_out, multiplexer_13_out, multiplexer_14_out,
       multiplexer_15_out, multiplexer_16_out, PC_1, PC_q, RF_A, RF_B, SyscallOut;
  wire [31:1] alu_1_result;
  wire [31:26] rom_1_data_2;

  Button \u_总复位  (.out(RST));
  Clock clock_1 (.out(clock_1_out));
  Button \u_单步执行  (.out(\单步执行_out ));
  Multiplexer #(.width(32), .enable("false")) multiplexer_1 (
    .in0(multiplexer_2_out), .in1(multiplexer_3_out), .out(multiplexer_1_out), .sel(control_signal[9]));
  // Probe on multiplexer_1_out
  not not_1 (not_1_out, halt);
  xor xor_1 (clk, clock_1_out, \单步执行_out );
  Multiplexer #(.width(32), .enable("false")) multiplexer_2 (
    .in0(PC_1), .in1(branch_addr), .out(multiplexer_2_out), .sel(branch));
  Multiplexer #(.width(32), .enable("false")) multiplexer_3 (
    .in0({PC_1[31:28], rom_1_data, 2'b00}), .in1(RF_A), .out(multiplexer_3_out), .sel(control_signal[8]));
  PC_1 pc_1_1 (.PC({PC_q[31:12], PC_q_2, PC_q[1:0]}), .PC_4(PC_1));
  Register #(.width(32)) PC (
    .D(multiplexer_1_out), .en(not_1_out), .Q({PC_q[31:12], PC_q_2, PC_q[1:0]}), .clk(clk), .clr(RST));
  Hex_Digit_Display hex_digit_display_1 (.value(SyscallOut[27:24]));  // open: dp
  Hex_Digit_Display hex_digit_display_2 (.value(SyscallOut[31:28]));  // open: dp
  Register #(.width(32)) \u_数码管锁存  (.D(RF_B), .en(display__a0), .Q(SyscallOut), .clk(clk), .clr(RST));
  Hex_Digit_Display hex_digit_display_3 (.value(SyscallOut[19:16]));  // open: dp
  Hex_Digit_Display hex_digit_display_4 (.value(SyscallOut[23:20]));  // open: dp
  ROM #(.addrWidth(10), .dataWidth(32)) rom_1 (.addr(PC_q_2), .data({rom_1_data_2, rom_1_data}));  // open: sel
  Hex_Digit_Display hex_digit_display_5 (.value(SyscallOut[15:12]));  // open: dp
  Hex_Digit_Display hex_digit_display_6 (.value(SyscallOut[11:8]));  // open: dp
  Hard_Wired_Controller hard_wired_controller_1 (
    .OP(rom_1_data_2), .Funct(rom_1_data[7:2]),
    .\控制信号 ({ALUOP, control_signal[23:8], beq, bne, bltz, control_signal[4:0]}));
  Hex_Digit_Display hex_digit_display_7 (.value(SyscallOut[7:4]));  // open: dp
  Hex_Digit_Display hex_digit_display_8 (.value(SyscallOut[3:0]));  // open: dp
  Multiplexer #(.width(5), .enable("false")) multiplexer_4 (
    .in0(rom_1_data[22:18]), .in1(rom_1_data[17:13]), .out(multiplexer_4_out), .sel(control_signal[21]));
  Multiplexer #(.width(17), .enable("false")) multiplexer_5 (
    .in0(17'ha), .in1({{12{1'b0}}, rom_1_data[12:8]}), .out(multiplexer_5_out), .sel(control_signal[12]));
  Multiplexer #(.width(17), .enable("false")) multiplexer_6 (
    .in0({{2{rom_1_data[17]}}, rom_1_data[16:2]}), .in1({1'b0, rom_1_data[17:2]}), .out(multiplexer_6_out),
    .sel(control_signal[10]));
  Multiplexer #(.width(32), .enable("false")) multiplexer_7 (
    .in0(multiplexer_12_out), .in1(multiplexer_13_out), .out(multiplexer_7_out), .sel(control_signal[17]));
  Multiplexer #(.width(5), .enable("false")) multiplexer_8 (
    .in0(rom_1_data[27:23]), .in1(5'b00010), .out(multiplexer_8_out), .sel(control_signal[23]));
  Multiplexer #(.width(5), .enable("false")) multiplexer_9 (
    .in0(rom_1_data[22:18]), .in1(5'b00100), .out(multiplexer_9_out), .sel(control_signal[22]));
  Multiplexer #(.width(5), .enable("false")) multiplexer_10 (
    .in0(multiplexer_4_out), .in1({5{1'b1}}), .out(multiplexer_10_out), .sel(control_signal[20]));
  Multiplexer #(.width(17), .enable("false")) multiplexer_11 (
    .in0(multiplexer_5_out), .in1(multiplexer_6_out), .out(multiplexer_11_out), .sel(control_signal[11]));
  Multiplexer #(.width(32), .enable("false")) multiplexer_12 (
    .in0({alu_1_result[31:26], alu_1_result_2, alu_1_result[1], ALU_R_0}), .in1(PC_1),
    .out(multiplexer_12_out), .sel(control_signal[18]));
  Multiplexer #(.width(32), .enable("false")) multiplexer_13 (
    .in0(mips_ram_1_p6), .in1({{16{1'b0}}, multiplexer_17_out}), .out(multiplexer_13_out),
    .sel(control_signal[16]));
  // Probe on multiplexer_10_out
  assign bit_extender_1_out = {{15{multiplexer_11_out[16]}}, multiplexer_11_out};  // Bit_Extender bit_extender_1
  // Probe on \总周期数 
  // Probe on \无条件分支指令数 
  // Probe on \有条件分支指令数 
  // Probe on \有条件分支成功跳转 
  // RegisterFile registerfile_1: pin names not known; wires that end beside it: multiplexer_7_out, clk, control_signal[19], multiplexer_10_out, multiplexer_8_out, multiplexer_9_out, RF_A, RF_B
  // Probe on multiplexer_9_out
  // Probe on multiplexer_8_out
  Multiplexer #(.width(32), .enable("false")) multiplexer_14 (
    .in0(RF_B), .in1(RF_A), .out(multiplexer_14_out), .sel(control_signal[14]));
  Adder #(.width(32)) adder_1 (.a(PC_1), .b({bit_extender_1_out[29:0], 2'b00}), .out(branch_addr));  // open: cin, cout
  Multiplexer #(.width(32), .enable("false")) multiplexer_15 (
    .in0(RF_A), .in1(RF_B), .out(multiplexer_15_out), .sel(control_signal[15]));
  ALU alu_1 (
    .AluOP(ALUOP), .X(multiplexer_15_out), .Equal(ALU_Equal),
    .Result({alu_1_result[31:26], alu_1_result_2, alu_1_result[1], ALU_R_0}), .Y(multiplexer_16_out));  // open: Signed_Overflow, Result_2, UnSigned_Overflow
  Multiplexer #(.width(32), .enable("false")) multiplexer_16 (
    .in0(multiplexer_14_out), .in1(bit_extender_1_out), .out(multiplexer_16_out), .sel(control_signal[13]));
  // MIPS_RAM mips_ram_1: pin names not known; wires that end beside it: alu_1_result_2, RF_B, control_signal[3], clk, RST, mips_ram_1_p6
  Multiplexer #(.width(16), .enable("false")) multiplexer_17 (
    .in0(mips_ram_1_p6[15:0]), .in1(mips_ram_1_p6[31:16]), .out(multiplexer_17_out), .sel(alu_1_result[1]));
  nor nor_1 (nor_1_out, control_signal[9], control_signal[8]);
  nor nor_2 (nor_2_out, beq, bne, bltz);
  not not_2 (not_2_out, branch);
  not not_3 (not_3_out, ALU_Equal);
  D_Flip_Flop d_ff_1 (.clk(clk), .D(halt), .Qn(d_ff_1_qn), .reset(RST));  // open: Q, preset, en
  D_Flip_Flop d_ff_2 (.clk(clk), .D(nor_1_out), .Qn(d_ff_2_qn), .preset(RST));  // open: Q, en, reset
  D_Flip_Flop d_ff_3 (.clk(clk), .D(nor_2_out), .Qn(d_ff_3_qn), .preset(RST));  // open: Q, en, reset
  D_Flip_Flop d_ff_4 (.clk(clk), .D(not_2_out), .Qn(d_ff_4_qn), .preset(RST));  // open: Q, en, reset
  and and_1 (halt, control_signal[4], ~not_3_out);  // AND_Gate
  and and_2 (display__a0, control_signal[4], not_3_out);
  and and_3 (and_3_out, ALU_Equal, beq);
  or or_1 (branch, and_3_out, and_4_out, and_5_out);
  and and_4 (and_4_out, ~ALU_Equal, bne);  // AND_Gate
  and and_5 (and_5_out, ALU_R_0, bltz);
  Counter #(.width(16), .max('hffff)) \u_总周期计数  (
    .count(d_ff_1_qn), .Q(\总周期数 ), .clk(clk), .clr(RST));  // open: load, D, carry
  Counter #(.width(16), .max('hffff)) \u_无条件分支指令计数  (
    .count(d_ff_2_qn), .Q(\无条件分支指令数 ), .clk(clk), .clr(RST));  // open: load, D, carry
  Counter #(.width(16), .max('hffff)) \u_有条件分支指令计数  (
    .count(d_ff_3_qn), .Q(\有条件分支指令数 ), .clk(clk), .clr(RST));  // open: load, D, carry
  Counter #(.width(16), .max('hffff)) \u_有条件分支成功跳转计数  (
    .count(d_ff_4_qn), .Q(\有条件分支成功跳转 ), .clk(clk), .clr(RST));  // open: load, D, carry

  // Other names for the same wires on the sheet: DM_WE = control_signal[3]; syscall = control_signal[4];
  //   control_signal (some bits) = {ALUOP, beq, bne, bltz}; jump_register = control_signal[8];
  //   jump = control_signal[9]; zero_ext_IMM = control_signal[10]; extend_IMM = control_signal[11];
  //   extend_shamt = control_signal[12]; Y__S_EXT = control_signal[13]; Y__RF_A = control_signal[14];
  //   X__RF_B = control_signal[15]; Din__DM_half = control_signal[16]; Din__DM = control_signal[17];
  //   Din__PC_1 = control_signal[18]; RF_WE = control_signal[19]; rW__GPR_31 = control_signal[20];
  //   rW__rd = control_signal[21]; rB___a0 = control_signal[22]; rA___v0 = control_signal[23]

  // Notes on the sheet:
  //   数码管输出应该用寄存器锁存，否则显示数据只能一闪而过
  //   指令存储器
  //   可以通过项目增加Logisim库的方式将前几次实验完成的电路作为子电路引入到本电路中使用
  //   contents of rom_1 (hex, n*v repeats v):
  //   20110001 8000c05 20110001 20120002 20130003 8000c09 20110001 20120002 20130003 8000c0d 20110001
  //   20120002 20130003 8000c11 20110001 20120002 20130003 c000cb8 20100001 20110001 118fc0 112020
  //   20020022 c 118882 12200001 8000c15 112020 20020022 c 20110001 118880 112020 20020022 c 12200001
  //   8000c1f 20110001 118fc0 112020 20020022 c 1188c3 112020 20020022 c 118903 112020 20020022 c 118903
  //   112020 20020022 c 118903 112020 20020022 c 118903 112020 20020022 c 118903 112020 20020022 c 118903
  //   112020 20020022 c 118903 112020 20020022 c 20100001 109fc0 139fc3 8021 2012000c 24160003 26100001
  //   3210000f 20080008 20090001 139900 2709825 132020 20020022 c 1094022 1500fff9 22100001 2018000f
  //   2188024 108700 20080008 20090001 139902 2709825 132021 20020022 c 1094022 1500fff9 108702 2c9b022
  //   12c00001 8000c50 4020 1084027 84400 3508ffff 82021 20020022 c 2010ffff 20110000 ae300000 22100001
  //   22310004 ae300000 22100001 22310004 ae300000 22100001 22310004 ae300000 22100001 22310004 ae300000
  //   22100001 22310004 ae300000 22100001 22310004 ae300000 22100001 22310004 ae300000 22100001 22310004
  //   ae300000 22100001 22310004 ae300000 22100001 22310004 ae300000 22100001 22310004 ae300000 22100001
  //   22310004 ae300000 22100001 22310004 ae300000 22100001 22310004 ae300000 22100001 22310004 ae300000
  //   22100001 22310004 22100001 8020 2011003c 8e130000 8e340000 274402a 11000002 ae330000 ae140000
  //   2231fffc 1611fff8 102020 20020022 c 22100004 2011003c 1611fff2 2002000a c 20100000 22100001 102020
  //   20020022 c 22100002 102020 20020022 c 22100003 102020 20020022 c 22100004 102020 20020022 c 22100005
  //   102020 20020022 c 22100006 102020 20020022 c 22100007 102020 20020022 c 22100008 102020 20020022
  //   20020022 c 3e00008
  //   数码管输出
  //   总复位信号应将除ROM以外所有存储组件全部清零
  //   寄存器堆
  //   数据存储器
endmodule

module PC_1 (
  input  [31:0] PC,
  output [31:0] PC_4
);

  // Incrementer incrementer_1: pin names not known; wires that end beside it: PC[31:2], PC_4[31:2]

  assign PC_4[1:0] = PC[1:0];
endmodule

module Hard_Wired_Controller (
  input  [5:0] OP,
  input  [5:0] Funct,
  output [27:0] \控制信号 
);

  wire add, addi, addiu, addu, \and , andi, comparator_1_eq, comparator_16_eq, comparator_17_eq,
       comparator_18_eq, comparator_19_eq, comparator_20_eq, comparator_21_eq, comparator_22_eq,
       comparator_23_eq, comparator_24_eq, comparator_25_eq, comparator_26_eq, comparator_27_eq,
       comparator_28_eq, comparator_29_eq, j, lw, \nor , \or , or_2_out, or_3_out, or_4_out, or_6_out,
       or_7_out, or_8_out, or_9_out, or_10_out, or_11_out, or_12_out, or_13_out, or_15_out, or_16_out,
       or_17_out, or_18_out, or_19_out, or_20_out, or_21_out, or_22_out, or_23_out, or_24_out, or_26_out,
       or_27_out, or_28_out, or_29_out, or_30_out, or_31_out, or_32_out, or_33_out, or_34_out, or_35_out,
       or_36_out, or_37_out, or_38_out, or_39_out, or_40_out, or_42_out, or_43_out, or_44_out, or_45_out,
       or_46_out, or_47_out, or_48_out, or_49_out, or_50_out, or_51_out, or_53_out, or_54_out, or_55_out,
       or_56_out, or_57_out, or_58_out, or_59_out, or_60_out, or_61_out, or_62_out, or_63_out, or_64_out,
       or_65_out, or_66_out, or_67_out, or_68_out, or_69_out, or_70_out, or_71_out, or_74_out, or_75_out,
       or_77_out, or_78_out, or_79_out, or_80_out, or_81_out, or_82_out, or_83_out, or_84_out, or_85_out,
       or_86_out, or_87_out, or_89_out, or_91_out, or_92_out, or_93_out, or_94_out, or_95_out, or_96_out,
       or_97_out, or_98_out, or_99_out, or_100_out, or_103_out, ori, sll, slt, slti, sltiu, sltu, sra, srl,
       sub;

  Comparator #(.width(6)) comparator_1 (.a(OP), .b({6{1'b0}}), .eq(comparator_1_eq));  // open: gt, lt
  Comparator #(.width(6)) comparator_2 (.a(OP), .b(6'b000001), .eq(\控制信号 [5]));  // open: gt, lt
  Comparator #(.width(6)) comparator_3 (.a(OP), .b(6'b000010), .eq(j));  // open: gt, lt
  Comparator #(.width(6)) comparator_4 (.a(OP), .b(6'b000011), .eq(\控制信号 [20]));  // open: gt, lt
  Comparator #(.width(6)) comparator_5 (.a(OP), .b(6'b000100), .eq(\控制信号 [7]));  // open: gt, lt
  Comparator #(.width(6)) comparator_6 (.a(OP), .b(6'b000101), .eq(\控制信号 [6]));  // open: gt, lt
  Comparator #(.width(6)) comparator_7 (.a(OP), .b(6'b001000), .eq(addi));  // open: gt, lt
  Comparator #(.width(6)) comparator_8 (.a(OP), .b(6'b001001), .eq(addiu));  // open: gt, lt
  Comparator #(.width(6)) comparator_9 (.a(OP), .b(6'b001010), .eq(slti));  // open: gt, lt
  Comparator #(.width(6)) comparator_10 (.a(OP), .b(6'b001011), .eq(sltiu));  // open: gt, lt
  Comparator #(.width(6)) comparator_11 (.a(OP), .b(6'b001100), .eq(andi));  // open: gt, lt
  Comparator #(.width(6)) comparator_12 (.a(OP), .b(6'b001101), .eq(ori));  // open: gt, lt
  Comparator #(.width(6)) comparator_13 (.a(OP), .b(6'b100001), .eq(\控制信号 [16]));  // open: gt, lt
  Comparator #(.width(6)) comparator_14 (.a(OP), .b(6'b100011), .eq(lw));  // open: gt, lt
  Comparator #(.width(6)) comparator_15 (.a(OP), .b(6'b101011), .eq(\控制信号 [3]));  // open: gt, lt
  Comparator #(.width(6)) comparator_16 (.a(Funct), .b({6{1'b0}}), .eq(comparator_16_eq));  // open: gt, lt
  Comparator #(.width(6)) comparator_17 (.a(Funct), .b(6'b000010), .eq(comparator_17_eq));  // open: gt, lt
  Comparator #(.width(6)) comparator_18 (.a(Funct), .b(6'b000011), .eq(comparator_18_eq));  // open: gt, lt
  Comparator #(.width(6)) comparator_19 (.a(Funct), .b(6'b000110), .eq(comparator_19_eq));  // open: gt, lt
  Comparator #(.width(6)) comparator_20 (.a(Funct), .b(6'b001000), .eq(comparator_20_eq));  // open: gt, lt
  Comparator #(.width(6)) comparator_21 (.a(Funct), .b(6'b001100), .eq(comparator_21_eq));  // open: gt, lt
  Comparator #(.width(6)) comparator_22 (.a(Funct), .b(6'b100000), .eq(comparator_22_eq));  // open: gt, lt
  Comparator #(.width(6)) comparator_23 (.a(Funct), .b(6'b100001), .eq(comparator_23_eq));  // open: gt, lt
  Comparator #(.width(6)) comparator_24 (.a(Funct), .b(6'b100010), .eq(comparator_24_eq));  // open: gt, lt
  Comparator #(.width(6)) comparator_25 (.a(Funct), .b(6'b100100), .eq(comparator_25_eq));  // open: gt, lt
  Comparator #(.width(6)) comparator_26 (.a(Funct), .b(6'b100101), .eq(comparator_26_eq));  // open: gt, lt
  Comparator #(.width(6)) comparator_27 (.a(Funct), .b(6'b100111), .eq(comparator_27_eq));  // open: gt, lt
  Comparator #(.width(6)) comparator_28 (.a(Funct), .b(6'b101010), .eq(comparator_28_eq));  // open: gt, lt
  Comparator #(.width(6)) comparator_29 (.a(Funct), .b(6'b101011), .eq(comparator_29_eq));  // open: gt, lt
  and and_1 (sll, comparator_1_eq, comparator_16_eq);
  and and_2 (srl, comparator_1_eq, comparator_17_eq);
  and and_3 (sra, comparator_1_eq, comparator_18_eq);
  and and_4 (\控制信号 [14], comparator_1_eq, comparator_19_eq);
  and and_5 (\控制信号 [8], comparator_1_eq, comparator_20_eq);
  and and_6 (\控制信号 [23], comparator_1_eq, comparator_21_eq);
  and and_7 (add, comparator_1_eq, comparator_22_eq);
  and and_8 (addu, comparator_1_eq, comparator_23_eq);
  and and_9 (sub, comparator_1_eq, comparator_24_eq);
  and and_10 (\and , comparator_1_eq, comparator_25_eq);
  and and_11 (\or , comparator_1_eq, comparator_26_eq);
  and and_12 (\nor , comparator_1_eq, comparator_27_eq);
  and and_13 (slt, comparator_1_eq, comparator_28_eq);
  and and_14 (sltu, comparator_1_eq, comparator_29_eq);
  or or_1 (\控制信号 [27], \or , or_6_out);
  or or_2 (or_2_out, slt, or_8_out);
  or or_3 (or_3_out, \控制信号 [5], or_10_out);
  or or_4 (or_4_out, sltiu, ori);
  // Probe on {\控制信号 [27:23], \控制信号 [23], \控制信号 [21:19], \控制信号 [20], \控制信号 [17:5], \控制信号 [23], \控制信号 [3], 3'b000}
  or or_5 (\控制信号 [26], \控制信号 [23], or_15_out);
  or or_6 (or_6_out, or_2_out, \nor );
  or or_7 (or_7_out, addu, or_17_out);
  or or_8 (or_8_out, or_3_out, sltu);
  or or_9 (or_9_out, \and , or_19_out);
  or or_10 (or_10_out, or_4_out, slti);
  or or_11 (or_11_out, addi, or_21_out);
  or or_12 (or_12_out, sltiu, or_23_out);
  or or_13 (or_13_out, \控制信号 [16], or_24_out);
  or or_14 (\控制信号 [25], srl, or_26_out);
  or or_15 (or_15_out, or_7_out, add);
  or or_16 (or_16_out, \控制信号 [23], or_28_out);
  or or_17 (or_17_out, or_9_out, sub);
  or or_18 (or_18_out, \and , or_30_out);
  or or_19 (or_19_out, or_11_out, sltu);
  or or_20 (or_20_out, slt, or_32_out);
  or or_21 (or_21_out, or_12_out, addiu);
  or or_22 (or_22_out, slti, andi);
  or or_23 (or_23_out, or_13_out, andi);
  or or_24 (or_24_out, lw, \控制信号 [3]);
  or or_25 (\控制信号 [24], sra, or_35_out);
  or or_26 (or_26_out, or_16_out, \控制信号 [14]);
  or or_27 (or_27_out, addu, or_36_out);
  or or_28 (or_28_out, or_18_out, sub);
  or or_29 (or_29_out, slt, or_37_out);
  or or_30 (or_30_out, or_20_out, \nor );
  or or_31 (or_31_out, addi, or_38_out);
  or or_32 (or_32_out, or_22_out, \控制信号 [5]);
  or or_33 (or_33_out, slti, or_39_out);
  or or_34 (or_34_out, \控制信号 [16], or_40_out);
  or or_35 (or_35_out, or_27_out, add);
  or or_36 (or_36_out, or_29_out, \and );
  or or_37 (or_37_out, or_31_out, \控制信号 [5]);
  or or_38 (or_38_out, or_33_out, addiu);
  or or_39 (or_39_out, or_34_out, andi);
  or or_40 (or_40_out, lw, \控制信号 [3]);
  or or_41 (\控制信号 [21], sll, or_42_out);
  or or_42 (or_42_out, or_43_out, srl);
  or or_43 (or_43_out, sra, or_44_out);
  or or_44 (or_44_out, or_45_out, \控制信号 [14]);
  or or_45 (or_45_out, add, or_46_out);
  or or_46 (or_46_out, or_47_out, addu);
  or or_47 (or_47_out, sub, or_48_out);
  or or_48 (or_48_out, or_49_out, \and );
  or or_49 (or_49_out, \or , or_50_out);
  or or_50 (or_50_out, or_51_out, \nor );
  or or_51 (or_51_out, slt, sltu);
  or or_52 (\控制信号 [19], sll, or_53_out);
  or or_53 (or_53_out, or_54_out, srl);
  or or_54 (or_54_out, sra, or_55_out);
  or or_55 (or_55_out, or_56_out, \控制信号 [14]);
  or or_56 (or_56_out, add, or_57_out);
  or or_57 (or_57_out, or_58_out, addu);
  or or_58 (or_58_out, sub, or_59_out);
  or or_59 (or_59_out, or_60_out, \and );
  or or_60 (or_60_out, \or , or_61_out);
  or or_61 (or_61_out, or_62_out, \nor );
  or or_62 (or_62_out, slt, or_63_out);
  or or_63 (or_63_out, or_64_out, sltu);
  or or_64 (or_64_out, \控制信号 [20], or_65_out);
  or or_65 (or_65_out, or_66_out, addi);
  or or_66 (or_66_out, addiu, or_67_out);
  or or_67 (or_67_out, or_68_out, slti);
  or or_68 (or_68_out, sltiu, or_69_out);
  or or_69 (or_69_out, or_70_out, andi);
  or or_70 (or_70_out, ori, or_71_out);
  or or_71 (or_71_out, \控制信号 [16], lw);
  or or_72 (\控制信号 [17], \控制信号 [16], lw);
  or or_73 (\控制信号 [15], sll, or_74_out);
  or or_74 (or_74_out, or_75_out, srl);
  or or_75 (or_75_out, sra, \控制信号 [14]);
  or or_76 (\控制信号 [13], sll, or_77_out);
  or or_77 (or_77_out, or_78_out, srl);
  or or_78 (or_78_out, sra, or_79_out);
  or or_79 (or_79_out, or_80_out, \控制信号 [23]);
  or or_80 (or_80_out, addi, or_81_out);
  or or_81 (or_81_out, or_82_out, addiu);
  or or_82 (or_82_out, slti, or_83_out);
  or or_83 (or_83_out, or_84_out, sltiu);
  or or_84 (or_84_out, andi, or_85_out);
  or or_85 (or_85_out, or_86_out, ori);
  or or_86 (or_86_out, \控制信号 [16], or_87_out);
  or or_87 (or_87_out, lw, \控制信号 [3]);
  or or_88 (\控制信号 [12], sll, or_89_out);
  or or_89 (or_89_out, srl, sra);
  or or_90 (\控制信号 [11], \控制信号 [5], or_91_out);
  or or_91 (or_91_out, or_92_out, \控制信号 [7]);
  or or_92 (or_92_out, \控制信号 [6], or_93_out);
  or or_93 (or_93_out, or_94_out, addi);
  or or_94 (or_94_out, addiu, or_95_out);
  or or_95 (or_95_out, or_96_out, slti);
  or or_96 (or_96_out, sltiu, or_97_out);
  or or_97 (or_97_out, or_98_out, andi);
  or or_98 (or_98_out, ori, or_99_out);
  or or_99 (or_99_out, or_100_out, \控制信号 [16]);
  or or_100 (or_100_out, lw, \控制信号 [3]);
  or or_101 (\控制信号 [10], andi, ori);
  or or_102 (\控制信号 [9], \控制信号 [8], or_103_out);
  or or_103 (or_103_out, j, \控制信号 [20]);

  assign {\控制信号 [22], \控制信号 [18], \控制信号 [4], \控制信号 [2:0]} = {\控制信号 [23], \控制信号 [20], \控制信号 [23], 3'b000};

  // Other names for the same wires on the sheet: sw = \控制信号 [3]; bltz = \控制信号 [5]; bne = \控制信号 [6]; beq = \控制信号 [7];
  //   jr = \控制信号 [8]; srlv = \控制信号 [14]; lh = \控制信号 [16]; jal = \控制信号 [20]; syscall = \控制信号 [23]
endmodule

module ROM_Controller (
  input  [5:0] OP,
  input  [5:0] Funct,
  output [27:0] \控制信号 
);

  ROM #(.addrWidth(12), .dataWidth(28)) rom_1 (.addr({OP, Funct}), .data(\控制信号 ));  // open: sel

  // Notes on the sheet:
  //   contents of rom_1 (hex, n*v repeats v):
  //   28b000 0 228b000 128b000 0 0 228c000 0 300 0 0 0 6c02010 19*0 5280000 5280000 6280000 0 7280000
  //   8280000 0 a280000 0 0 b280000 c280000 20*0 64*b000820 64*200 64*1c0200 64*880 64*840 128*0
  //   128*5082800 64*b082800 64*c082800 64*7082c00 64*8082c00 1216*0 64*50b2800 64*0 64*50a2800 448*0
  //   64*5002808
endmodule
