// Logisim project 区位码转GB2312机内码.circ as structural Verilog: 1 circuit, main circuit main
module main (
  input  in_1,
  input  in_2
);

  wire clock_1_out;
  wire [7:0] counter_1_q, multiplier_1_out, multiplier_2_out;
  wire [15:0] adder_1_out, adder_3_out, rom_1_data;

  Counter counter_1 (.Q(counter_1_q), .clk(clock_1_out), .clr(in_1));  // open: load, D, count, carry
  Clock clock_1 (.out(clock_1_out));
  ROM #(.dataWidth(16)) rom_1 (.addr(counter_1_q), .data(rom_1_data));  // open: sel
  RAM #(.dataWidth(16), .bus("separate")) ram_1 (
    .addr(counter_1_q), .din(adder_3_out), .str(in_2), .clk(clock_1_out));  // open: data, sel, ld, clr
  Multiplier multiplier_1 (.a(8'ha), .b({4'b0000, rom_1_data[7:4]}), .out(multiplier_1_out));  // open: cin, cout
  Adder adder_1 (.a({4'b0000, rom_1_data[3:0]}), .b(multiplier_1_out), .out(adder_1_out[7:0]));  // open: cin, cout
  Adder adder_2 (.a({4'b0000, rom_1_data[11:8]}), .b(multiplier_2_out), .out(adder_1_out[15:8]));  // open: cin, cout
  Multiplier multiplier_2 (.a(8'ha), .b({4'b0000, rom_1_data[15:12]}), .out(multiplier_2_out));  // open: cin, cout
  Adder #(.width(16)) adder_3 (.a(adder_1_out), .b(16'ha0a0), .out(adder_3_out));  // open: cin, cout

  // Notes on the sheet:
  //   contents of rom_1 (hex, n*v repeats v):
  //   2838 4367 2790 3138 4907 5175 2828 4285
endmodule
